# Fritzing sketch timer_lcd (saved by Fritzing 0.3.19b)
breadboards: 1

parts:
  LCD1 = LCD screen
  Arduino1 = Arduino
  S1 = Pushbutton [package="[THT]"]
  S2 = Pushbutton [package="[THT]"]
  S3 = Pushbutton [package="[THT]"]
  S4 = Pushbutton [package="[THT]"]
  R1 = Resistor [resistance=10k package=THT]
  R2 = Resistor [resistance=10k package=THT]
  R3 = Resistor [resistance=10k package=THT]
  R4 = Resistor [resistance=10k package=THT]

nets:
  N1: LCD1.VSS, LCD1.V0, LCD1.R/W, R1.Pin_0, R2.Pin_0, R3.Pin_0, R4.Pin_0
  VDD: LCD1.VDD, Arduino1.+5V, S1.Pin_3, S1.Pin_4, S2.Pin_3, S2.Pin_4, S3.Pin_3, S3.Pin_4, S4.Pin_3, S4.Pin_4
  N2: LCD1.RS, Arduino1.D12
  N3: LCD1.E, Arduino1.D11
  N4: LCD1.DB6, Arduino1.D5
  N5: LCD1.DB7, Arduino1.D4
  N6: LCD1.LED+, Arduino1.D3
  N7: LCD1.LED-, Arduino1.D2
  N8: Arduino1.D9, S1.Pin_1, S1.Pin_2, R1.Pin_1
  N9: Arduino1.D8, S2.Pin_1, S2.Pin_2, R2.Pin_1
  N10: Arduino1.D7, S3.Pin_1, S3.Pin_2, R3.Pin_1
  N11: Arduino1.D6, S4.Pin_1, S4.Pin_2, R4.Pin_1
